# Fritzing sketch SketchESP8268-01 (saved by Fritzing 0.9.3b)
breadboards: 1

parts:
  Composant1 = FTDI Basic Programmer
  Composant2 = BME280 Breakout  # not connected
  S3 = Pushbutton [package="[SMD]"]
  Espessif_Serial_Wifi_Modul_1 = ESP8266 ESP01 [part_number=ESP8266 package=THT]

nets:
  N1: Composant1.RXI, Espessif_Serial_Wifi_Modul_1.TXD
  N2: Composant1.TXO, Espessif_Serial_Wifi_Modul_1.RXD
  N3: Composant1.POWER, Espessif_Serial_Wifi_Modul_1.VCC
  N4: Composant1.GND, S3.Pin_3, S3.Pin_4
  N5: S3.Pin_1, S3.Pin_2, Espessif_Serial_Wifi_Modul_1.GPIO00

custom parts:
  ESP8266 ESP01: Generic WiFi Module based on the ESP8266 with onboard PCB antenna and UART communications
