# Fritzing sketch SketchESP8268-NodeMcu (saved by Fritzing 0.9.3b)
breadboards: 1

parts:
  Adafruit_HUZZAH_ESP8266_Breakout1 = Adafruit HUZZAH ESP8266 Breakout [part_number=2471]  # not connected
  Composant1 = FTDI Basic Programmer  # not connected
  Composant2 = BME280 Breakout  # not connected
  S3 = Pushbutton [package="[SMD]"]

nets:
  N1: S3.Pin_1, S3.Pin_2
  N2: S3.Pin_3, S3.Pin_4
